// Logisim project PLDs.circ as structural Verilog: 33 circuits, main circuit AR_LD_PLD
module AR_LD_PLD (
  input  t0,
  input  t2,
  input  t4,
  input  clock,
  input  d01,
  input  d02,
  output AR_LD_OUT
);

  wire and_1_out, not_1_out, or_1_out, or_2_out;

  not not_1 (not_1_out, clock);
  or or_1 (or_1_out, d01, d02);
  and and_1 (and_1_out, t4, or_1_out);
  or or_2 (or_2_out, t0, t2, and_1_out);
  and and_2 (AR_LD_OUT, or_2_out, not_1_out);

  // Notes on the sheet:
  //   CLA 8
  //   Collin Hatcher
  //   Noah Brown
endmodule

module PC_BUS_PLD (
  input  t0,
  input  t2,
  output PC_BUS_OUT
);

  or or_1 (PC_BUS_OUT, t0, t2);
endmodule

module PC_LD_PLD (
  input  t4,
  input  clock,
  input  d05,
  input  d06,
  input  z,
  output PC_LD_OUT
);

  wire and_1_out, not_1_out, or_1_out;

  not not_1 (not_1_out, clock);
  or or_1 (or_1_out, d05, and_1_out);
  and and_1 (and_1_out, d06, z);
  and and_2 (PC_LD_OUT, t4, or_1_out, not_1_out);
endmodule

module PC_INC_S1 (
  input  d01,
  input  d02,
  input  d06,
  input  z,
  output PC_INC_t3_ds
);

  wire and_1_out, not_1_out;

  not not_1 (not_1_out, z);
  and and_1 (and_1_out, d06, not_1_out);
  or or_1 (PC_INC_t3_ds, d01, d02, and_1_out);
endmodule

module PC_INC_S2 (
  input  t1,
  input  t3,
  input  t3_ds,
  input  clock,
  output PC_INC_OUT
);

  wire and_1_out, not_1_out;

  not not_1 (not_1_out, clock);
  and and_1 (and_1_out, t3, t3_ds, not_1_out);
  or or_1 (PC_INC_OUT, t1, and_1_out);
endmodule

module PC_INC_PLD (
  input  t1,
  input  t3,
  input  clock,
  input  d01,
  input  d02,
  input  d06,
  input  z,
  output PC_INC_OUT
);

  wire pc_inc_s1_1_pc_inc_t3_ds;

  PC_INC_S1 pc_inc_s1_1 (.d01(d01), .d02(d02), .d06(d06), .z(z), .PC_INC_t3_ds(pc_inc_s1_1_pc_inc_t3_ds));
  PC_INC_S2 pc_inc_s2_1 (.t1(t1), .t3(t3), .t3_ds(pc_inc_s1_1_pc_inc_t3_ds), .clock(clock), .PC_INC_OUT(PC_INC_OUT));
endmodule

module DR_LD_S1 (
  input  d01,
  input  d02,
  input  t3,
  input  t5,
  output DR_LD_OUT1
);

  wire or_1_out, or_2_out;

  or or_1 (or_1_out, d01, d02);
  or or_2 (or_2_out, t3, t5);
  and and_1 (DR_LD_OUT1, or_1_out, or_2_out);
endmodule

module DR_LD_S2 (
  input  d05,
  input  d06,
  input  z,
  output DR_LD_OUT2
);

  wire and_1_out;

  and and_1 (and_1_out, z, d06);
  or or_1 (DR_LD_OUT2, d05, and_1_out);
endmodule

module DR_LD_S3 (
  input  t1,
  input  DR_LD_OUT1,
  input  t3,
  input  DR_LD_OUT2,
  input  clock,
  output DR_LD_OUT
);

  wire and_1_out, not_1_out, or_1_out;

  not not_1 (not_1_out, clock);
  and and_1 (and_1_out, t3, DR_LD_OUT2);
  or or_1 (or_1_out, t1, DR_LD_OUT1, and_1_out);
  and and_2 (DR_LD_OUT, or_1_out, not_1_out);
endmodule

module DR_LD_PLD (
  input  t1,
  input  t3,
  input  t5,
  input  clock,
  input  d01,
  input  d02,
  input  d05,
  input  d06,
  input  z,
  output DR_LD_OUT
);

  wire dr_ld_s1_1_dr_ld_out1, dr_ld_s2_1_dr_ld_out2;

  DR_LD_S1 dr_ld_s1_1 (.d01(d01), .d02(d02), .t3(t3), .t5(t5), .DR_LD_OUT1(dr_ld_s1_1_dr_ld_out1));
  DR_LD_S2 dr_ld_s2_1 (.d05(d05), .d06(d06), .z(z), .DR_LD_OUT2(dr_ld_s2_1_dr_ld_out2));
  DR_LD_S3 dr_ld_s3_1 (
    .t1(t1), .DR_LD_OUT1(dr_ld_s1_1_dr_ld_out1), .t3(t3), .DR_LD_OUT2(dr_ld_s2_1_dr_ld_out2), .clock(clock),
    .DR_LD_OUT(DR_LD_OUT));
endmodule

module R_LD_PLD (
  input  t3,
  input  clock,
  input  d03,
  output R_LD_OUT
);

  wire not_1_out;

  not not_1 (not_1_out, clock);
  and and_1 (R_LD_OUT, t3, d03, not_1_out);
endmodule

module S_LD_PLD (
  input  t3,
  input  clock,
  input  d00,
  output S_LD_OUT
);

  wire not_1_out;

  not not_1 (not_1_out, clock);
  and and_1 (S_LD_OUT, t3, d00, not_1_out);
endmodule

module ACC_CLR_PLD (
  input  t3,
  input  d11,
  output ACC_CLR_OUT
);

  and and_1 (ACC_CLR_OUT, t3, d11);
endmodule

module ACC_BUS_PLD (
  input  t3,
  input  t5,
  input  d02,
  input  d03,
  input  d07,
  output ACC_BUS_OUT
);

  wire and_1_out, and_2_out, or_1_out;

  or or_1 (or_1_out, d03, d07);
  and and_1 (and_1_out, t5, d02);
  and and_2 (and_2_out, t3, or_1_out);
  or or_2 (ACC_BUS_OUT, and_1_out, and_2_out);
endmodule

module Z_LD_PLD (
  output Z_LD_OUT
);


  assign Z_LD_OUT = 1'b1;
endmodule

module OUTR_LD_PLD (
  input  t3,
  input  clock,
  input  d07,
  output OUTR_LD_OUT
);

  wire not_1_out;

  not not_1 (not_1_out, clock);
  and and_1 (OUTR_LD_OUT, d07, t3, not_1_out);
endmodule

module RAM_WE_PLD (
  input  t6,
  input  clock,
  input  d02,
  output RAM_WE_OUT
);

  wire not_1_out;

  not not_1 (not_1_out, clock);
  and and_1 (RAM_WE_OUT, d02, t6, not_1_out);
endmodule

module IR_LD_PLD (
  input  t2,
  input  clock,
  output IR_LD_OUT
);

  wire not_1_out;

  not not_1 (not_1_out, clock);
  and and_1 (IR_LD_OUT, t2, not_1_out);
endmodule

module DR_BUS_S1 (
  input  t4,
  input  t6,
  input  d01,
  input  d02,
  output DR_BUS_SUB1_OUT
);

  wire or_1_out, or_2_out;

  or or_1 (or_1_out, d01, d02);
  or or_2 (or_2_out, t4, t6);
  and and_1 (DR_BUS_SUB1_OUT, or_1_out, or_2_out);
endmodule

module DR_BUS_S2 (
  input  t4,
  input  d05,
  input  d06,
  input  z,
  input  DR_BUS_SUB1_OUT,
  output DR_BUS_OUT
);

  wire and_1_out, and_2_out, or_1_out;

  and and_1 (and_1_out, z, d06);
  or or_1 (or_1_out, d05, and_1_out);
  or or_2 (DR_BUS_OUT, DR_BUS_SUB1_OUT, and_2_out);
  and and_2 (and_2_out, t4, or_1_out);
endmodule

module DR_BUS_PLD (
  input  t4,
  input  t6,
  input  d01,
  input  d02,
  input  d05,
  input  d06,
  input  z,
  output DR_BUS_OUT
);

  wire dr_bus_s1_1_dr_bus_sub1_out;

  DR_BUS_S1 dr_bus_s1_1 (.t4(t4), .t6(t6), .d01(d01), .d02(d02), .DR_BUS_SUB1_OUT(dr_bus_s1_1_dr_bus_sub1_out));
  DR_BUS_S2 dr_bus_s2_1 (
    .t4(t4), .d05(d05), .d06(d06), .z(z), .DR_BUS_SUB1_OUT(dr_bus_s1_1_dr_bus_sub1_out),
    .DR_BUS_OUT(DR_BUS_OUT));
endmodule

module R_BUS_PLD (
  input  t3,
  input  d04,
  input  d08,
  input  d09,
  input  d12,
  input  d13,
  output R_BUS_OUT
);

  wire or_1_out;

  and and_1 (R_BUS_OUT, t3, or_1_out);
  or or_1 (or_1_out, d04, d08, d09, d12, d13);
endmodule

module ACC_LD_S1 (
  input  d04,
  input  d08,
  input  d09,
  input  d10,
  output ACC_LD_SUB1_OUT
);

  or or_1 (ACC_LD_SUB1_OUT, d04, d08, d09, d10);
endmodule

module ACC_LD_S2 (
  input  d12,
  input  d13,
  input  d14,
  input  d15,
  output ACC_LD_SUB2_OUT
);

  or or_1 (ACC_LD_SUB2_OUT, d12, d13, d14, d15);
endmodule

module ACC_LD_S3 (
  input  t3,
  input  t6,
  input  clock,
  input  d01,
  input  ACC_SUB1_OUT,
  input  ACC_SUB2_OUT,
  output ACC_LD_SUB3_OUT
);

  wire and_1_out, and_2_out, not_1_out, or_1_out, or_2_out;

  not not_1 (not_1_out, clock);
  or or_1 (or_1_out, ACC_SUB1_OUT, ACC_SUB2_OUT);
  and and_1 (and_1_out, t3, or_1_out);
  or or_2 (or_2_out, and_1_out, and_2_out);
  and and_2 (and_2_out, t6, d01);
  and and_3 (ACC_LD_SUB3_OUT, or_2_out, not_1_out);
endmodule

module ACC_LD_PLD (
  input  t3,
  input  t6,
  input  clock,
  input  d01,
  input  d04,
  input  d08,
  input  d09,
  input  d10,
  input  d12,
  input  d13,
  input  d14,
  input  d15,
  output ACC_LD_OUT
);

  wire acc_ld_s1_1_acc_ld_sub1_out, acc_ld_s2_1_acc_ld_sub2_out;

  ACC_LD_S1 acc_ld_s1_1 (.d04(d04), .d08(d08), .d09(d09), .d10(d10), .ACC_LD_SUB1_OUT(acc_ld_s1_1_acc_ld_sub1_out));
  ACC_LD_S2 acc_ld_s2_1 (.d12(d12), .d13(d13), .d14(d14), .d15(d15), .ACC_LD_SUB2_OUT(acc_ld_s2_1_acc_ld_sub2_out));
  ACC_LD_S3 acc_ld_s3_1 (
    .t3(t3), .t6(t6), .clock(clock), .d01(d01), .ACC_SUB1_OUT(acc_ld_s1_1_acc_ld_sub1_out),
    .ACC_SUB2_OUT(acc_ld_s2_1_acc_ld_sub2_out), .ACC_LD_SUB3_OUT(ACC_LD_OUT));
endmodule

module ALU_SEL_PLD (
  input  d01,
  input  d04,
  input  d09,
  input  d10,
  input  d12,
  input  d13,
  input  d14,
  input  d15,
  output s0,
  output s1,
  output s2
);

  wire or_1_out;

  or or_1 (or_1_out, d01, d04);
  or or_2 (s0, d15, d13, d09, or_1_out);
  or or_3 (s1, d10, d14, d15, or_1_out);
  or or_4 (s2, d12, d13, d14, d15);
endmodule

module RAM_OE_S1 (
  input  d01,
  input  d02,
  input  d05,
  input  d06,
  input  z,
  output RAM_OE_SUB1_OUT
);

  wire and_1_out;

  and and_1 (and_1_out, d06, z);
  or or_1 (RAM_OE_SUB1_OUT, d01, d02, d05, and_1_out);
endmodule

module RAM_OE_S2 (
  input  t1,
  input  t3,
  input  t5,
  input  clock,
  input  d01,
  input  RAM_OE_SUB1_OUT,
  output RAM_OE_SUB2_OUT
);

  wire and_1_out, and_2_out, not_1_out, or_1_out;

  not not_1 (not_1_out, clock);
  and and_1 (and_1_out, d01, t5);
  and and_2 (and_2_out, t3, RAM_OE_SUB1_OUT);
  or or_1 (or_1_out, t1, and_1_out, and_2_out);
  and and_3 (RAM_OE_SUB2_OUT, or_1_out, not_1_out);
endmodule

module RAM_OE_PLD (
  input  t1,
  input  t3,
  input  t5,
  input  clock,
  input  d01,
  input  d02,
  input  d05,
  input  d06,
  input  z,
  output RAM_OE_OUT
);

  wire ram_oe_s1_1_ram_oe_sub1_out;

  RAM_OE_S1 ram_oe_s1_1 (
    .d01(d01), .d02(d02), .d05(d05), .d06(d06), .z(z), .RAM_OE_SUB1_OUT(ram_oe_s1_1_ram_oe_sub1_out));
  RAM_OE_S2 ram_oe_s2_1 (
    .t1(t1), .t3(t3), .t5(t5), .clock(clock), .d01(d01), .RAM_OE_SUB1_OUT(ram_oe_s1_1_ram_oe_sub1_out),
    .RAM_OE_SUB2_OUT(RAM_OE_OUT));
endmodule

module SC_CLR_S1 (
  input  t4,
  input  d01,
  input  d02,
  input  d05,
  input  d06,
  input  z,
  output SC_CLR_SUB1_OUT
);

  wire and_1_out, nor_1_out;

  and and_1 (and_1_out, d06, z);
  nor nor_1 (nor_1_out, d01, d02, d05, and_1_out);
  and and_2 (SC_CLR_SUB1_OUT, t4, nor_1_out);
endmodule

module SC_CLR_S2 (
  input  t5,
  input  t7,
  input  SC_CLR_SUB1_OUT,
  input  d05,
  input  d06,
  input  z,
  output SC_CLR_SUB2_OUT
);

  wire and_1_out, and_2_out, or_1_out;

  and and_1 (and_1_out, d06, z);
  or or_1 (or_1_out, d05, and_1_out);
  and and_2 (and_2_out, t5, or_1_out);
  or or_2 (SC_CLR_SUB2_OUT, SC_CLR_SUB1_OUT, and_2_out, t7);
endmodule

module SC_CLR_PLD (
  input  t4,
  input  t5,
  input  t7,
  input  d01,
  input  d02,
  input  d05,
  input  d06,
  input  z,
  output SC_CLR_OUT
);

  wire sc_clr_s1_1_sc_clr_sub1_out;

  SC_CLR_S1 sc_clr_s1_1 (
    .t4(t4), .d01(d01), .d02(d02), .d05(d05), .d06(d06), .z(z), .SC_CLR_SUB1_OUT(sc_clr_s1_1_sc_clr_sub1_out));
  SC_CLR_S2 sc_clr_s2_1 (
    .t5(t5), .t7(t7), .SC_CLR_SUB1_OUT(sc_clr_s1_1_sc_clr_sub1_out), .d05(d05), .d06(d06), .z(z),
    .SC_CLR_SUB2_OUT(SC_CLR_OUT));
endmodule
