// Logisim project RSC.circ as structural Verilog: 10 circuits, main circuit Arith_U
// AU
module Arith_U (
  input  [31:0] A,
  input  [31:0] B,
  input  S1,
  input  S0,
  output [31:0] AU_out
);

  wire and_1_out, nor_1_out;
  wire [31:0] adder_1_out, multiplexer_1_out, not_1_out;

  assign not_1_out = ~B;  // NOT_Gate not_1, 32 bits wide
  Multiplexer #(.select(2), .width(32)) multiplexer_1 (
    .in0(not_1_out), .in1(B), .in2(32'h1), .in3(B), .out(multiplexer_1_out), .sel({S1, S0}));
  nor nor_1 (nor_1_out, S0, S1);
  Adder #(.width(32)) adder_1 (.a(A), .b(multiplexer_1_out), .out(adder_1_out), .cin(nor_1_out));  // open: cout
  and and_1 (and_1_out, S1, S0);
  Multiplexer #(.width(32)) multiplexer_2 (.in0(adder_1_out), .in1(B), .out(AU_out), .sel(and_1_out));

  // Notes on the sheet:
  //   CLA#6
  //   Collin Hatcher
  //   Noah Brown
  //   0      0
  //   0      1
  //   1      0
  //   1       1
  //   s1    s0      output
  //   7e117a1e
  //   c0cac01a
  //   9f6eldld
  //   215ca2fe
endmodule

// LU
module Logic_U (
  input  [31:0] A,
  input  [31:0] B,
  input  S1,
  input  S0,
  output [31:0] Logic_Out
);

  wire [31:0] and_1_out, not_1_out, or_1_out, shifter_1_out;

  assign not_1_out = ~A;  // NOT_Gate not_1, 32 bits wide
  assign and_1_out = B & A;  // AND_Gate and_1, 32 bits wide
  assign or_1_out = A | B;  // OR_Gate or_1, 32 bits wide
  Shifter #(.shift("ar"), .width(32)) shifter_1 (.in(A), .\dist (5'b00001), .out(shifter_1_out));
  Multiplexer #(.select(2), .width(32)) multiplexer_1 (
    .in0(and_1_out), .in1(or_1_out), .in2(shifter_1_out), .in3(not_1_out), .out(Logic_Out), .sel({S1, S0}));

  // Notes on the sheet:
  //   CLA#6
  //   Collin Hatcher
  //   Noah Brown
endmodule

module ALU (
  input  [31:0] A,
  input  [31:0] B,
  input  S2,
  input  S1,
  input  S0,
  output [31:0] ALU_Out
);

  wire [31:0] arith_u_1_au_out, logic_u_1_logic_out;

  Arith_U arith_u_1 (.A(A), .B(B), .S1(S1), .S0(S0), .AU_out(arith_u_1_au_out));
  Logic_U logic_u_1 (.A(A), .B(B), .S1(S1), .S0(S0), .Logic_Out(logic_u_1_logic_out));
  Multiplexer #(.width(32)) multiplexer_1 (.in0(arith_u_1_au_out), .in1(logic_u_1_logic_out), .out(ALU_Out), .sel(S2));

  // Notes on the sheet:
  //   Collin Hatcher
  //   Noah Brown
  //   CLA#6
endmodule

module SC (
  input  Clock,
  input  Clear,
  output [2:0] SEQ_out
);

  wire [2:0] adder_1_out;

  Adder #(.width(3)) adder_1 (.a(SEQ_out), .b(3'b001), .out(adder_1_out));  // open: cin, cout
  Register #(.width(3)) register_1 (.D(adder_1_out), .clk(Clock), .Q(SEQ_out), .clr(Clear));  // open: en

  // Notes on the sheet:
  //   CLA#6
  //   Collin Hatcher
  //   Noah Brown
endmodule

module DecoderCircut (
  input  [31:0] IR_In,
  output [15:0] D_Out,
  output [3:0] Debug_Instructions
);

  wire multiplexer_1_out, nor_1_out, or_2_out, or_3_out;
  wire [7:0] or_1_out;

  assign or_1_out = IR_In[15:8] | IR_In[23:16] | IR_In[31:24];  // OR_Gate or_1, 8 bits wide
  or or_2 (or_2_out, IR_In[4], IR_In[5], IR_In[6], IR_In[7]);
  or or_3 (or_3_out, or_1_out[0], or_1_out[1], or_1_out[2], or_1_out[3], or_1_out[4], or_1_out[5], or_1_out[6], or_1_out[7]);
  Decoder #(.select(4)) decoder_1 (
    .out0(D_Out[0]), .out1(D_Out[1]), .out2(D_Out[2]), .out3(D_Out[3]), .out4(D_Out[4]), .out5(D_Out[5]),
    .out6(D_Out[6]), .out7(D_Out[7]), .out8(D_Out[8]), .out9(D_Out[9]), .out10(D_Out[10]), .out11(D_Out[11]),
    .out12(D_Out[12]), .out13(D_Out[13]), .out14(D_Out[14]), .out15(D_Out[15]), .sel(IR_In[3:0]),
    .en(multiplexer_1_out));
  Multiplexer multiplexer_1 (.in0(1'b0), .in1(1'b1), .out(multiplexer_1_out), .sel(nor_1_out));
  nor nor_1 (nor_1_out, or_2_out, or_3_out);

  assign Debug_Instructions = IR_In[3:0];

  // Notes on the sheet:
  //   CLA#7
  //   Collin Hatcher
  //   Noah Brown
endmodule

module TimerCircut (
  input  Clock,
  input  Clear,
  input  Stop,
  output [7:0] T_Out
);

  wire [2:0] sc_1_seq_out;
  wire [7:0] decoder_1_out0;

  SC sc_1 (.Clock(Clock), .Clear(Clear), .SEQ_out(sc_1_seq_out));
  Decoder #(.select(3)) decoder_1 (
    .out0(decoder_1_out0[0]), .out1(decoder_1_out0[1]), .out2(decoder_1_out0[2]), .out3(decoder_1_out0[3]),
    .out4(decoder_1_out0[4]), .out5(decoder_1_out0[5]), .out6(decoder_1_out0[6]), .out7(decoder_1_out0[7]),
    .sel(sc_1_seq_out));  // open: en
  Multiplexer #(.width(8)) multiplexer_1 (.in0(decoder_1_out0), .in1({8{1'b0}}), .out(T_Out), .sel(Stop));

  // Notes on the sheet:
  //   CLA#7
  //   Collin Hatcher
  //   Noah Brown
endmodule

module RSC (
  output [7:0] out_1,
  output [3:0] out_2
);

  wire control_1_acc_bus, control_1_acc_clr, control_1_acc_ld, control_1_ar_ld, control_1_dr_bus,
       control_1_dr_ld, control_1_ir_ld, control_1_outr_ld, control_1_pc_bus, control_1_pc_inc,
       control_1_pc_ld, control_1_r_bus, control_1_r_ld, control_1_ram_oe, control_1_ram_we, control_1_z_ld,
       Primary_Clock_out, z_reg_1_z_out;
  wire [2:0] control_1_alu_s;
  wire [31:0] acc_1_out_put, alu_1_alu_out, ar_1_out_put, dr_1_out_put, ir_1_out_put, outr_1_out_put,
       pc_1_out_put, r_1_bus_output, r_1_out_put;

  Control control_1 (
    .Clock(Primary_Clock_out), .Z_IN(z_reg_1_z_out), .IR_IN(ir_1_out_put), .IR_LD(control_1_ir_ld),
    .T(out_1), .RAM_WE(control_1_ram_we), .RAM_OE(control_1_ram_oe), .D(out_2), .AR_LD(control_1_ar_ld),
    .PC_LD(control_1_pc_ld), .PC_INC(control_1_pc_inc), .PC_BUS(control_1_pc_bus), .DR_LD(control_1_dr_ld),
    .DR_BUS(control_1_dr_bus), .R_LD(control_1_r_ld), .R_BUS(control_1_r_bus), .ACC_LD(control_1_acc_ld),
    .ACC_CLR(control_1_acc_clr), .ACC_BUS(control_1_acc_bus), .ALU_S(control_1_alu_s),
    .OUTR_LD(control_1_outr_ld), .Z_LD(control_1_z_ld));
  // Probe on control_1_ar_ld
  // Probe on control_1_z_ld
  Clock Primary_Clock (.out(Primary_Clock_out));
  // Probe on r_1_bus_output
  ALU alu_1 (
    .A(acc_1_out_put), .B(r_1_bus_output), .S2(control_1_alu_s[2]), .S1(control_1_alu_s[1]),
    .S0(control_1_alu_s[0]), .ALU_Out(alu_1_alu_out));
  Z_Reg z_reg_1 (.Clock(Primary_Clock_out), .ACC_in(acc_1_out_put), .Load(control_1_z_ld), .Z_out(z_reg_1_z_out));
  // Probe on ar_1_out_put
  AR ar_1 (.Data(r_1_bus_output), .load(control_1_ar_ld), .Clock(Primary_Clock_out), .OUT_PUT(ar_1_out_put));
  R r_1 (
    .Data(r_1_bus_output), .load(control_1_r_ld), .Clock(Primary_Clock_out), .Bus_enable(control_1_r_bus),
    .OUT_PUT(r_1_out_put), .Bus_output(r_1_bus_output));
  // Probe on alu_1_alu_out
  RAM #(.addrWidth(16), .dataWidth(32), .databus("bidir"), .trigger("high")) ram_1 (
    .addr(ar_1_out_put[15:0]), .we(control_1_ram_we), .oe(control_1_ram_oe), .data(r_1_bus_output));
  DR dr_1 (
    .Data(r_1_bus_output), .load(control_1_dr_ld), .Clock(Primary_Clock_out), .Bus_enable(control_1_dr_bus),
    .OUT_PUT(dr_1_out_put), .Bus_output(r_1_bus_output));
  // Probe on r_1_out_put
  // Probe on acc_1_out_put
  // Probe on dr_1_out_put
  PC pc_1 (
    .Data(r_1_bus_output), .count(control_1_pc_inc), .load(control_1_pc_ld), .Clock(Primary_Clock_out),
    .Bus_Enable(control_1_pc_bus), .OUT_PUT(pc_1_out_put), .Bus_Output(r_1_bus_output));
  ACC acc_1 (
    .Data(alu_1_alu_out), .load(control_1_acc_ld), .Clock(Primary_Clock_out), .clear(control_1_acc_clr),
    .Bus_enable(control_1_acc_bus), .OUT_PUT(acc_1_out_put), .Bus_output(r_1_bus_output));
  // Probe on pc_1_out_put
  IR ir_1 (.Data(dr_1_out_put), .load(control_1_ir_ld), .Clock(Primary_Clock_out), .OUT_PUT(ir_1_out_put));
  OUTR outr_1 (.Data(r_1_bus_output), .load(control_1_outr_ld), .Clock(Primary_Clock_out), .OUT_PUT(outr_1_out_put));
  // Probe on ir_1_out_put
  Hex_Digit_Display hex_digit_display_1 (.value(outr_1_out_put[31:28]));  // open: dp
  Hex_Digit_Display hex_digit_display_2 (.value(outr_1_out_put[27:24]));  // open: dp
  Hex_Digit_Display hex_digit_display_3 (.value(outr_1_out_put[23:20]));  // open: dp
  Hex_Digit_Display hex_digit_display_4 (.value(outr_1_out_put[19:16]));  // open: dp
  Hex_Digit_Display hex_digit_display_5 (.value(outr_1_out_put[15:12]));  // open: dp
  Hex_Digit_Display hex_digit_display_6 (.value(outr_1_out_put[11:8]));  // open: dp
  Hex_Digit_Display hex_digit_display_7 (.value(outr_1_out_put[7:4]));  // open: dp
  Hex_Digit_Display hex_digit_display_8 (.value(outr_1_out_put[3:0]));  // open: dp

  // Notes on the sheet:
  //   Noah Brown
  //   OLA #8
endmodule

module Z_Reg (
  input  Clock,
  input  [31:0] ACC_in,
  input  Load,
  output Z_out
);

  wire not_1_out, or_1_out;

  or or_1 (or_1_out, ACC_in[0], ACC_in[1], ACC_in[2], ACC_in[3], ACC_in[4], ACC_in[5], ACC_in[6], ACC_in[7], ACC_in[8], ACC_in[9], ACC_in[10], ACC_in[11], ACC_in[12], ACC_in[13], ACC_in[14], ACC_in[15], ACC_in[17], ACC_in[18], ACC_in[19], ACC_in[20], ACC_in[21], ACC_in[22], ACC_in[23], ACC_in[24], ACC_in[25], ACC_in[26], ACC_in[27], ACC_in[28], ACC_in[29], ACC_in[30], ACC_in[31], ACC_in[16]);
  not not_1 (not_1_out, or_1_out);
  Onebit_reg onebit_reg_1 (.Clock(Clock), .Data(not_1_out), .Clear(1'b0), .Load(Load), .Data_Out(Z_out));
endmodule

module Control (
  input  Clock,
  input  Z_IN,
  input  [31:0] IR_IN,
  output IR_LD,
  output [7:0] T,
  output RAM_WE,
  output RAM_OE,
  output [3:0] D,
  output AR_LD,
  output PC_LD,
  output PC_INC,
  output PC_BUS,
  output DR_LD,
  output DR_BUS,
  output R_LD,
  output R_BUS,
  output ACC_LD,
  output ACC_CLR,
  output ACC_BUS,
  output [2:0] ALU_S,
  output OUTR_LD,
  output Z_LD
);

  wire s_ld_pld_1_s_ld_out, s_reg_1_data_out, sc_clr_pld_1_sc_clr_out;
  wire [15:0] decodercircut_1_d_out;

  S_Reg s_reg_1 (.Clock(Clock), .Load(s_ld_pld_1_s_ld_out), .Data_out(s_reg_1_data_out));
  TimerCircut timercircut_1 (.Clock(Clock), .Clear(sc_clr_pld_1_sc_clr_out), .Stop(s_reg_1_data_out), .T_Out(T));
  DecoderCircut decodercircut_1 (.IR_In(IR_IN), .D_Out(decodercircut_1_d_out), .Debug_Instructions(D));
  IR_LD_PLD ir_ld_pld_1 (.t2(T[2]), .clock(Clock), .IR_LD_OUT(IR_LD));
  RAM_WE_PLD ram_we_pld_1 (.t6(T[6]), .clock(Clock), .d02(decodercircut_1_d_out[2]), .RAM_WE_OUT(RAM_WE));
  RAM_OE_PLD ram_oe_pld_1 (
    .t1(T[1]), .t3(T[3]), .t5(T[5]), .clock(Clock), .d01(decodercircut_1_d_out[1]),
    .d02(decodercircut_1_d_out[2]), .d05(decodercircut_1_d_out[5]), .d06(decodercircut_1_d_out[6]), .z(Z_IN),
    .RAM_OE_OUT(RAM_OE));
  AR_LD_PLD ar_ld_pld_1 (
    .t0(T[0]), .t2(T[2]), .t4(T[4]), .clock(Clock), .d01(decodercircut_1_d_out[1]),
    .d02(decodercircut_1_d_out[2]), .AR_LD_OUT(AR_LD));
  PC_LD_PLD pc_ld_pld_1 (
    .t4(T[4]), .clock(Clock), .d05(decodercircut_1_d_out[5]), .d06(decodercircut_1_d_out[6]), .z(Z_IN),
    .PC_LD_OUT(PC_LD));
  PC_INC_PLD pc_inc_pld_1 (
    .t1(T[1]), .t3(T[3]), .clock(Clock), .d01(decodercircut_1_d_out[1]), .d02(decodercircut_1_d_out[2]),
    .d06(decodercircut_1_d_out[6]), .z(Z_IN), .PC_INC_OUT(PC_INC));
  PC_BUS_PLD pc_bus_pld_1 (.t0(T[0]), .t2(T[2]), .PC_BUS_OUT(PC_BUS));
  DR_LD_PLD dr_ld_pld_1 (
    .t1(T[1]), .t3(T[3]), .t5(T[5]), .clock(Clock), .d01(decodercircut_1_d_out[1]),
    .d02(decodercircut_1_d_out[2]), .d05(decodercircut_1_d_out[5]), .d06(decodercircut_1_d_out[6]), .z(Z_IN),
    .DR_LD_OUT(DR_LD));
  DR_BUS_PLD dr_bus_pld_1 (
    .t4(T[4]), .t6(T[6]), .d01(decodercircut_1_d_out[1]), .d02(decodercircut_1_d_out[2]),
    .d05(decodercircut_1_d_out[5]), .d06(decodercircut_1_d_out[6]), .z(Z_IN), .DR_BUS_OUT(DR_BUS));
  R_LD_PLD r_ld_pld_1 (.t3(T[3]), .clock(Clock), .d03(decodercircut_1_d_out[3]), .R_LD_OUT(R_LD));
  R_BUS_PLD r_bus_pld_1 (
    .t3(T[3]), .d04(decodercircut_1_d_out[4]), .d08(decodercircut_1_d_out[8]),
    .d09(decodercircut_1_d_out[9]), .d12(decodercircut_1_d_out[12]), .d13(decodercircut_1_d_out[13]),
    .R_BUS_OUT(R_BUS));
  ACC_LD_PLD acc_ld_pld_1 (
    .t3(T[3]), .t6(T[6]), .clock(Clock), .d01(decodercircut_1_d_out[1]), .d04(decodercircut_1_d_out[4]),
    .d08(decodercircut_1_d_out[8]), .d09(decodercircut_1_d_out[9]), .d10(decodercircut_1_d_out[10]),
    .d12(decodercircut_1_d_out[12]), .d13(decodercircut_1_d_out[13]), .d14(decodercircut_1_d_out[14]),
    .d15(decodercircut_1_d_out[15]), .ACC_LD_OUT(ACC_LD));
  ACC_CLR_PLD acc_clr_pld_1 (.t3(T[3]), .d11(decodercircut_1_d_out[11]), .ACC_CLR_OUT(ACC_CLR));
  ACC_BUS_PLD acc_bus_pld_1 (
    .t3(T[3]), .t5(T[5]), .d02(decodercircut_1_d_out[2]), .d03(decodercircut_1_d_out[3]),
    .d07(decodercircut_1_d_out[7]), .ACC_BUS_OUT(ACC_BUS));
  ALU_SEL_PLD alu_sel_pld_1 (
    .d01(decodercircut_1_d_out[1]), .d04(decodercircut_1_d_out[4]), .d09(decodercircut_1_d_out[9]),
    .d10(decodercircut_1_d_out[10]), .d12(decodercircut_1_d_out[12]), .d13(decodercircut_1_d_out[13]),
    .d14(decodercircut_1_d_out[14]), .d15(decodercircut_1_d_out[15]), .s0(ALU_S[0]), .s1(ALU_S[1]),
    .s2(ALU_S[2]));
  OUTR_LD_PLD outr_ld_pld_1 (.t3(T[3]), .clock(Clock), .d07(decodercircut_1_d_out[7]), .OUTR_LD_OUT(OUTR_LD));
  Z_LD_PLD z_ld_pld_1 (.Z_LD_OUT(Z_LD));
  SC_CLR_PLD sc_clr_pld_1 (
    .t4(T[4]), .t5(T[5]), .t7(T[7]), .d01(decodercircut_1_d_out[1]), .d02(decodercircut_1_d_out[2]),
    .d05(decodercircut_1_d_out[5]), .d06(decodercircut_1_d_out[6]), .z(Z_IN),
    .SC_CLR_OUT(sc_clr_pld_1_sc_clr_out));
  S_LD_PLD s_ld_pld_1 (.t3(T[3]), .clock(Clock), .d00(decodercircut_1_d_out[0]), .S_LD_OUT(s_ld_pld_1_s_ld_out));

  // Notes on the sheet:
  //   TSIGNALS
  //   D Signals
endmodule

module S_Reg (
  input  Clock,
  input  Load,
  output Data_out
);

  Onebit_reg onebit_reg_1 (.Clock(Clock), .Data(1'b1), .Clear(1'b0), .Load(Load), .Data_Out(Data_out));
endmodule
