// Logisim project custom_reg.circ as structural Verilog: 12 circuits, main circuit Onebit_reg
module Onebit_reg (
  input  Clock,
  input  Data,
  input  Clear,
  input  Load,
  output Data_Out
);

  wire and_1_out, and_2_out, not_1_out;

  not not_1 (not_1_out, Data);
  J_K_Flip_Flop j_k_ff_1 (
    .J(and_1_out), .K(and_2_out), .clk(Clock), .Q(Data_Out), .preset(1'b0), .reset(Clear));  // open: Qn
  and and_1 (and_1_out, Data, Load);
  and and_2 (and_2_out, not_1_out, Load);

  // Notes on the sheet:
  //   One bit Register
endmodule

module BasicRegister (
  input  [31:0] Data_In,
  input  load,
  input  Clock,
  output [31:0] Data_Out
);

  Register #(.width(32)) register_1 (.D(Data_In), .en(load), .clk(Clock), .Q(Data_Out));  // open: clr
endmodule

module BusRegister (
  input  [31:0] Data_In,
  input  load,
  input  Clock,
  input  Bus_Enable,
  output [31:0] Data_Out,
  output [31:0] Bus_Out
);

  Register #(.width(32)) register_1 (.D(Data_In), .en(load), .clk(Clock), .Q(Data_Out));  // open: clr
  assign Bus_Out = Bus_Enable ? Data_Out : 32'bz;  // Controlled_Buffer controlled_buffer_1
endmodule

module ClearRegister (
  input  [31:0] Data_In,
  input  load,
  input  Clock,
  input  Clear,
  input  Bus_Enable,
  output [31:0] Data_Out,
  output [31:0] Bus_Out
);

  Register #(.width(32)) register_1 (.D(Data_In), .en(load), .clk(Clock), .Q(Data_Out), .clr(Clear));
  assign Bus_Out = Bus_Enable ? Data_Out : 32'bz;  // Controlled_Buffer controlled_buffer_1
endmodule

module CountRegister (
  input  [31:0] Data_In,
  input  count,
  input  load,
  input  Clock,
  input  Bus_Enable,
  output [31:0] Data_Out,
  output [31:0] Bus_Out
);

  wire or_1_out;
  wire [31:0] adder_1_out, multiplexer_1_out;

  Adder #(.width(32)) adder_1 (.a(Data_Out), .b(32'h1), .out(adder_1_out));  // open: cin, cout
  or or_1 (or_1_out, count, load);
  Multiplexer #(.width(32)) multiplexer_1 (.in0(Data_In), .in1(adder_1_out), .out(multiplexer_1_out), .sel(count));
  Register #(.width(32)) register_1 (.D(multiplexer_1_out), .en(or_1_out), .clk(Clock), .Q(Data_Out));  // open: clr
  assign Bus_Out = Bus_Enable ? Data_Out : 32'bz;  // Controlled_Buffer controlled_buffer_1
endmodule

module ACC (
  input  [31:0] Data,
  input  load,
  input  Clock,
  input  clear,
  input  Bus_enable,
  output [31:0] OUT_PUT,
  output [31:0] Bus_output
);

  ClearRegister clearregister_1 (
    .Data_In(Data), .load(load), .Clock(Clock), .Clear(clear), .Bus_Enable(Bus_enable), .Data_Out(OUT_PUT),
    .Bus_Out(Bus_output));
endmodule

module AR (
  input  [31:0] Data,
  input  load,
  input  Clock,
  output [31:0] OUT_PUT
);

  BasicRegister basicregister_1 (.Data_In(Data), .load(load), .Clock(Clock), .Data_Out(OUT_PUT));
endmodule

module DR (
  input  [31:0] Data,
  input  load,
  input  Clock,
  input  Bus_enable,
  output [31:0] OUT_PUT,
  output [31:0] Bus_output
);

  BusRegister busregister_1 (
    .Data_In(Data), .load(load), .Clock(Clock), .Bus_Enable(Bus_enable), .Data_Out(OUT_PUT),
    .Bus_Out(Bus_output));
endmodule

module IR (
  input  [31:0] Data,
  input  load,
  input  Clock,
  output [31:0] OUT_PUT
);

  BasicRegister basicregister_1 (.Data_In(Data), .load(load), .Clock(Clock), .Data_Out(OUT_PUT));
endmodule

module OUTR (
  input  [31:0] Data,
  input  load,
  input  Clock,
  output [31:0] OUT_PUT
);

  BasicRegister basicregister_1 (.Data_In(Data), .load(load), .Clock(Clock), .Data_Out(OUT_PUT));
endmodule

module PC (
  input  [31:0] Data,
  input  count,
  input  load,
  input  Clock,
  input  Bus_Enable,
  output [31:0] OUT_PUT,
  output [31:0] Bus_Output
);

  CountRegister countregister_1 (
    .Data_In(Data), .count(count), .load(load), .Clock(Clock), .Bus_Enable(Bus_Enable), .Data_Out(OUT_PUT),
    .Bus_Out(Bus_Output));
endmodule

module R (
  input  [31:0] Data,
  input  load,
  input  Clock,
  input  Bus_enable,
  output [31:0] OUT_PUT,
  output [31:0] Bus_output
);

  BusRegister busregister_1 (
    .Data_In(Data), .load(load), .Clock(Clock), .Bus_Enable(Bus_enable), .Data_Out(OUT_PUT),
    .Bus_Out(Bus_output));
endmodule
